# Fritzing sketch Schematic (saved by Fritzing 0.9.3b)
breadboards: 1

parts:
  WeMos_D1_Mini1 = WeMos D1 Mini
  U1 = LCD-16X2 [package=lcd-16x2]
  R1 = Resistor [tolerance=±5% resistance=220 package=THT]
  R2 = Trimmer Potentiometer [maximum_resistance=10kΩ package=THT]  # not connected

nets:
  5V: WeMos_D1_Mini1.5V, U1.VDD, R1.Pin_1
  N1: WeMos_D1_Mini1.D1, U1.RS
  N2: WeMos_D1_Mini1.D2, U1.E
  N3: WeMos_D1_Mini1.D3, U1.DB4
  N4: WeMos_D1_Mini1.D4, U1.DB5
  N5: WeMos_D1_Mini1.D5, U1.DB6
  N6: WeMos_D1_Mini1.D6, U1.DB7
  N7: WeMos_D1_Mini1.G, U1.VSS, U1.R_W, U1.K
  N8: U1.A, R1.Pin_0
