# Fritzing sketch Schematic (saved by Fritzing 0.9.3b)

parts:
  WeMos_D1_Mini1 = WeMos D1 Mini
  RHT1 = Humidity and Temperature Sensor RHT03

nets:
  5V: WeMos_D1_Mini1.5V, RHT1.Vcc
  N1: WeMos_D1_Mini1.D4, RHT1.Data-signal
  N2: WeMos_D1_Mini1.G, RHT1.GND_1
